# Fritzing sketch A-Few-Pixels (saved by Fritzing 0.9.3b)

parts:
  Raspberry_Pi_1 = Raspberry Pi 3 [part_number=RPI-3-V1.2]
  Part1 = NeoPixel Stick [part_number=1426]

nets:
  GND: Raspberry_Pi_1.GND, Part1.GND
  N1: Raspberry_Pi_1.GIPO18, Part1.DATAIN
  5V: Raspberry_Pi_1.5V, Part1.+5V

notes:
  To power around eight Neopixels we can use the following diagram. This can be powered up to full brightness (255) but reader discretion is advised as they are VERY bright.

custom parts:
  NeoPixel Stick: Make your own little LED strip arrangement with this stick of NeoPixel LEDs. We crammed 8 of the tiny 5050 (5mm x 5mm) smart RGB LEDs onto a PCB with mounting holes and a chainable design. Use only one microcontroller pin to control as many as you can chain together! Each LED is addressable as the driver chip is inside the LED. Each one has ~18mA constant current drive so the color will be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
