# Fritzing sketch Lots-of-pixels (saved by Fritzing 0.9.3b)

parts:
  NEOPIXEL1 = Neopixel Strip -- White (60/m)
  Raspberry_Pi_1 = Raspberry Pi 3 [part_number=RPI-3-V1.2]
  VCC1 = 4 x AAA Battery Mount

nets:
  N1: NEOPIXEL1.DI, Raspberry_Pi_1.GIPO18
  GND: NEOPIXEL1.GND, Raspberry_Pi_1.GND, VCC1.-

notes:
  If powering a lot of Neopixels or using them at full brightness then use an external 5v 4A power supply.
  Attach them to the strip and Pi as per this diagram.

custom parts:
  Neopixel Strip -- White (60/m): Neopixel Strip, White, 60 pixels per meter.
